// Digital circuit circuito_exp3_simulacao.dig as structural Verilog
module circuito_exp3_simulacao (
  input  Reset,
  input  Iniciar,
  input  [3:0] Chaves
);

  wire Clock_out, u_circuito_exp3_db_igual, u_circuito_exp3_db_iniciar, u_circuito_exp3_pronto,
       u_Split7Bit_2_bit0, u_Split7Bit_2_bit1, u_Split7Bit_2_bit2, u_Split7Bit_2_bit3, u_Split7Bit_2_bit4,
       u_Split7Bit_2_bit5, u_Split7Bit_2_bit6, u_Split7Bit_3_bit0, u_Split7Bit_3_bit1, u_Split7Bit_3_bit2,
       u_Split7Bit_3_bit3, u_Split7Bit_3_bit4, u_Split7Bit_3_bit5, u_Split7Bit_3_bit6, u_Split7Bit_4_bit0,
       u_Split7Bit_4_bit1, u_Split7Bit_4_bit2, u_Split7Bit_4_bit3, u_Split7Bit_4_bit4, u_Split7Bit_4_bit5,
       u_Split7Bit_4_bit6, u_Split7Bit_bit0, u_Split7Bit_bit1, u_Split7Bit_bit2, u_Split7Bit_bit3,
       u_Split7Bit_bit4, u_Split7Bit_bit5, u_Split7Bit_bit6;
  wire [6:0] u_circuito_exp3_db_chaves, u_circuito_exp3_db_contagem, u_circuito_exp3_db_estado,
       u_circuito_exp3_db_memoria;

  Button Clock (.out(Clock_out));
  circuito_exp3 #(.applicationType("IVERILOG"), .CodeFile("/home/thaylor/Poli/labdig/exp3/arquivos_exp3/circuito_exp3_combined.v")) u_circuito_exp3 (
    .clock(Clock_out), .reset(Reset), .iniciar(Iniciar), .chaves(Chaves), .pronto(u_circuito_exp3_pronto),
    .db_igual(u_circuito_exp3_db_igual), .db_iniciar(u_circuito_exp3_db_iniciar),
    .db_contagem(u_circuito_exp3_db_contagem), .db_memoria(u_circuito_exp3_db_memoria),
    .db_chaves(u_circuito_exp3_db_chaves), .db_estado(u_circuito_exp3_db_estado));
  Split7Bit #(.applicationType("IVERILOG")) u_Split7Bit (
    .word_in(u_circuito_exp3_db_estado), .bit0(u_Split7Bit_bit0), .bit1(u_Split7Bit_bit1),
    .bit2(u_Split7Bit_bit2), .bit3(u_Split7Bit_bit3), .bit4(u_Split7Bit_bit4), .bit5(u_Split7Bit_bit5),
    .bit6(u_Split7Bit_bit6));
  LED Pronto (.in(u_circuito_exp3_pronto));
  LED Igual (.in(u_circuito_exp3_db_igual));
  LED u_Iniciar (.in(u_circuito_exp3_db_iniciar));
  Seven_Seg seven_seg_1 (
    .a(u_Split7Bit_bit0), .b(u_Split7Bit_bit1), .c(u_Split7Bit_bit2), .d(u_Split7Bit_bit3),
    .e(u_Split7Bit_bit4), .f(u_Split7Bit_bit5), .g(u_Split7Bit_bit6), .dp(1'b0));
  Split7Bit #(.applicationType("IVERILOG")) u_Split7Bit_2 (
    .word_in(u_circuito_exp3_db_contagem), .bit0(u_Split7Bit_2_bit0), .bit1(u_Split7Bit_2_bit1),
    .bit2(u_Split7Bit_2_bit2), .bit3(u_Split7Bit_2_bit3), .bit4(u_Split7Bit_2_bit4),
    .bit5(u_Split7Bit_2_bit5), .bit6(u_Split7Bit_2_bit6));
  Split7Bit #(.applicationType("IVERILOG")) u_Split7Bit_3 (
    .word_in(u_circuito_exp3_db_memoria), .bit0(u_Split7Bit_3_bit0), .bit1(u_Split7Bit_3_bit1),
    .bit2(u_Split7Bit_3_bit2), .bit3(u_Split7Bit_3_bit3), .bit4(u_Split7Bit_3_bit4),
    .bit5(u_Split7Bit_3_bit5), .bit6(u_Split7Bit_3_bit6));
  Split7Bit #(.applicationType("IVERILOG")) u_Split7Bit_4 (
    .word_in(u_circuito_exp3_db_chaves), .bit0(u_Split7Bit_4_bit0), .bit1(u_Split7Bit_4_bit1),
    .bit2(u_Split7Bit_4_bit2), .bit3(u_Split7Bit_4_bit3), .bit4(u_Split7Bit_4_bit4),
    .bit5(u_Split7Bit_4_bit5), .bit6(u_Split7Bit_4_bit6));
  Seven_Seg seven_seg_2 (
    .a(u_Split7Bit_2_bit0), .b(u_Split7Bit_2_bit1), .c(u_Split7Bit_2_bit2), .d(u_Split7Bit_2_bit3),
    .e(u_Split7Bit_2_bit4), .f(u_Split7Bit_2_bit5), .g(u_Split7Bit_2_bit6), .dp(1'b0));
  Seven_Seg seven_seg_3 (
    .a(u_Split7Bit_3_bit0), .b(u_Split7Bit_3_bit1), .c(u_Split7Bit_3_bit2), .d(u_Split7Bit_3_bit3),
    .e(u_Split7Bit_3_bit4), .f(u_Split7Bit_3_bit5), .g(u_Split7Bit_3_bit6), .dp(1'b0));
  Seven_Seg seven_seg_4 (
    .a(u_Split7Bit_4_bit0), .b(u_Split7Bit_4_bit1), .c(u_Split7Bit_4_bit2), .d(u_Split7Bit_4_bit3),
    .e(u_Split7Bit_4_bit4), .f(u_Split7Bit_4_bit5), .g(u_Split7Bit_4_bit6), .dp(1'b0));
endmodule

/* Code of Split7Bit:
module Split7Bit (
    input [6:0] word_in,      // 7-bit input
    output bit0,              // Outputs individual bits
    output bit1,
    output bit2,
    output bit3,
    output bit4,
    output bit5,
    output bit6
);

    assign bit0 = ~word_in[0]; // Assign each bit from the input word to an individual output
    assign bit1 = ~word_in[1];
    assign bit2 = ~word_in[2];
    assign bit3 = ~word_in[3];
    assign bit4 = ~word_in[4];
    assign bit5 = ~word_in[5];
    assign bit6 = ~word_in[6];

endmodule
*/
