// Digital circuit fluxo_dados_simulacao.dig as structural Verilog
module fluxo_dados_simulacao (
  input  [3:0] Chaves,
  input  ZeraRegistrador,
  input  Registra,
  input  Conta,
  input  ZeraContador,
  output [3:0] Contagem,
  output [3:0] Registrador,
  output [3:0] Memoria
);

  wire Clock_out, u_exp3_fluxo_dados_chavesigualmemoria, u_exp3_fluxo_dados_fimc;

  Button Clock (.out(Clock_out));
  exp3_fluxo_dados #(.applicationType("IVERILOG"), .CodeFile("/home/thaylor/Poli/labdig/exp3/simulacao/fluxo_dados_combined.v")) u_exp3_fluxo_dados (
    .clock(Clock_out), .chaves(Chaves), .zeraR(ZeraRegistrador), .registraR(Registra), .contaC(Conta),
    .zeraC(ZeraContador), .chavesIgualMemoria(u_exp3_fluxo_dados_chavesigualmemoria),
    .fimC(u_exp3_fluxo_dados_fimc), .db_contagem(Contagem), .db_chaves(Registrador), .db_memoria(Memoria));
  LED Igual (.in(u_exp3_fluxo_dados_chavesigualmemoria));
  LED Fim (.in(u_exp3_fluxo_dados_fimc));
endmodule
