// Digital circuit exp5_T5BB5_digital.dig as structural Verilog
module exp5_T5BB5_digital (
  input  Clock_1KHz,
  input  dificuldada,
  output [3:0] ledsChaves,
  output Igual,
  output [6:0] Contagem,
  output [6:0] Memoria,
  output [6:0] Estado,
  output [6:0] JogadaFeita,
  output dbClock,
  output dbIniciar,
  output TemJogada,
  output [6:0] Limite,
  output dificuldade
);

  wire Chave0_out, Chave1_out, Chave2_out, Chave3_out, Iniciar_out, Reset_out, u_circuito_exp5_acertou,
       u_circuito_exp5_db_timeout, u_circuito_exp5_errou, u_circuito_exp5_pronto, u_Split7Bit_2_bit0,
       u_Split7Bit_2_bit1, u_Split7Bit_2_bit2, u_Split7Bit_2_bit3, u_Split7Bit_2_bit4, u_Split7Bit_2_bit5,
       u_Split7Bit_2_bit6, u_Split7Bit_3_bit0, u_Split7Bit_3_bit1, u_Split7Bit_3_bit2, u_Split7Bit_3_bit3,
       u_Split7Bit_3_bit4, u_Split7Bit_3_bit5, u_Split7Bit_3_bit6, u_Split7Bit_4_bit0, u_Split7Bit_4_bit1,
       u_Split7Bit_4_bit2, u_Split7Bit_4_bit3, u_Split7Bit_4_bit4, u_Split7Bit_4_bit5, u_Split7Bit_4_bit6,
       u_Split7Bit_5_bit0, u_Split7Bit_5_bit1, u_Split7Bit_5_bit2, u_Split7Bit_5_bit3, u_Split7Bit_5_bit4,
       u_Split7Bit_5_bit5, u_Split7Bit_5_bit6, u_Split7Bit_bit0, u_Split7Bit_bit1, u_Split7Bit_bit2,
       u_Split7Bit_bit3, u_Split7Bit_bit4, u_Split7Bit_bit5, u_Split7Bit_bit6;
  wire [3:0] u_jointBit_chaves_out;

  Button Chave0 (.out(Chave0_out));
  Button Chave1 (.out(Chave1_out));
  Button Chave2 (.out(Chave2_out));
  Button Chave3 (.out(Chave3_out));
  jointBit #(.applicationType("IVERILOG")) u_jointBit (
    .chaves0(Chave0_out), .chaves1(Chave1_out), .chaves2(Chave2_out), .chaves3(Chave3_out),
    .chaves_out(u_jointBit_chaves_out));
  Split7Bit #(.applicationType("IVERILOG")) u_Split7Bit (
    .word_in(Limite), .bit0(u_Split7Bit_bit0), .bit1(u_Split7Bit_bit1), .bit2(u_Split7Bit_bit2),
    .bit3(u_Split7Bit_bit3), .bit4(u_Split7Bit_bit4), .bit5(u_Split7Bit_bit5), .bit6(u_Split7Bit_bit6));
  Button Reset (.out(Reset_out));
  Button Iniciar (.out(Iniciar_out));
  circuito_exp5 #(.applicationType("IVERILOG"), .CodeFile("/home/thaylor/Poli/labdig/LabDig-Aulas/exp5/simulacao/circuito_exp5_combined.v")) u_circuito_exp5 (
    .clock(Clock_1KHz), .reset(Reset_out), .iniciar(Iniciar_out), .botoes(u_jointBit_chaves_out),
    .botaoDificuldade(dificuldada), .acertou(u_circuito_exp5_acertou), .errou(u_circuito_exp5_errou),
    .pronto(u_circuito_exp5_pronto), .leds(ledsChaves), .db_igual(Igual), .db_contagem(Contagem),
    .db_memoria(Memoria), .db_estado(Estado), .db_jogadafeita(JogadaFeita), .db_limite(Limite),
    .db_clock(dbClock), .db_iniciar(dbIniciar), .db_tem_jogada(TemJogada),
    .db_timeout(u_circuito_exp5_db_timeout), .db_dificuldade(dificuldade));
  Seven_Seg seven_seg_1 (
    .a(u_Split7Bit_bit0), .b(u_Split7Bit_bit1), .c(u_Split7Bit_bit2), .d(u_Split7Bit_bit3),
    .e(u_Split7Bit_bit4), .f(u_Split7Bit_bit5), .g(u_Split7Bit_bit6), .dp(1'b0));
  Split7Bit #(.applicationType("IVERILOG")) u_Split7Bit_2 (
    .word_in(JogadaFeita), .bit0(u_Split7Bit_2_bit0), .bit1(u_Split7Bit_2_bit1), .bit2(u_Split7Bit_2_bit2),
    .bit3(u_Split7Bit_2_bit3), .bit4(u_Split7Bit_2_bit4), .bit5(u_Split7Bit_2_bit5), .bit6(u_Split7Bit_2_bit6));
  Seven_Seg seven_seg_2 (
    .a(u_Split7Bit_2_bit0), .b(u_Split7Bit_2_bit1), .c(u_Split7Bit_2_bit2), .d(u_Split7Bit_2_bit3),
    .e(u_Split7Bit_2_bit4), .f(u_Split7Bit_2_bit5), .g(u_Split7Bit_2_bit6), .dp(1'b0));
  LED Acertou (.in(u_circuito_exp5_acertou));
  LED Errou (.in(u_circuito_exp5_errou));
  LED Pronto (.in(u_circuito_exp5_pronto));
  LED dbTimeout (.in(u_circuito_exp5_db_timeout));
  Split7Bit #(.applicationType("IVERILOG")) u_Split7Bit_3 (
    .word_in(Estado), .bit0(u_Split7Bit_3_bit0), .bit1(u_Split7Bit_3_bit1), .bit2(u_Split7Bit_3_bit2),
    .bit3(u_Split7Bit_3_bit3), .bit4(u_Split7Bit_3_bit4), .bit5(u_Split7Bit_3_bit5), .bit6(u_Split7Bit_3_bit6));
  Split7Bit #(.applicationType("IVERILOG")) u_Split7Bit_4 (
    .word_in(Contagem), .bit0(u_Split7Bit_4_bit0), .bit1(u_Split7Bit_4_bit1), .bit2(u_Split7Bit_4_bit2),
    .bit3(u_Split7Bit_4_bit3), .bit4(u_Split7Bit_4_bit4), .bit5(u_Split7Bit_4_bit5), .bit6(u_Split7Bit_4_bit6));
  Split7Bit #(.applicationType("IVERILOG")) u_Split7Bit_5 (
    .word_in(Memoria), .bit0(u_Split7Bit_5_bit0), .bit1(u_Split7Bit_5_bit1), .bit2(u_Split7Bit_5_bit2),
    .bit3(u_Split7Bit_5_bit3), .bit4(u_Split7Bit_5_bit4), .bit5(u_Split7Bit_5_bit5), .bit6(u_Split7Bit_5_bit6));
  Seven_Seg seven_seg_3 (
    .a(u_Split7Bit_3_bit0), .b(u_Split7Bit_3_bit1), .c(u_Split7Bit_3_bit2), .d(u_Split7Bit_3_bit3),
    .e(u_Split7Bit_3_bit4), .f(u_Split7Bit_3_bit5), .g(u_Split7Bit_3_bit6), .dp(1'b0));
  Seven_Seg seven_seg_4 (
    .a(u_Split7Bit_4_bit0), .b(u_Split7Bit_4_bit1), .c(u_Split7Bit_4_bit2), .d(u_Split7Bit_4_bit3),
    .e(u_Split7Bit_4_bit4), .f(u_Split7Bit_4_bit5), .g(u_Split7Bit_4_bit6), .dp(1'b0));
  Seven_Seg seven_seg_5 (
    .a(u_Split7Bit_5_bit0), .b(u_Split7Bit_5_bit1), .c(u_Split7Bit_5_bit2), .d(u_Split7Bit_5_bit3),
    .e(u_Split7Bit_5_bit4), .f(u_Split7Bit_5_bit5), .g(u_Split7Bit_5_bit6), .dp(1'b0));

  // Notes on the sheet:
  //   Clock_1KHz: Hz: 1000
endmodule

/* Code of jointBit:
module jointBit (
    input chaves0,
    input chaves1,
    input chaves2,
    input chaves3,
    output [3:0] chaves_out
);

	assign chaves_out = {chaves3, chaves2, chaves1, chaves0};

endmodule
*/

/* Code of Split7Bit:
module Split7Bit (
    input [6:0] word_in,      // 7-bit input
    output bit0,              // Outputs individual bits
    output bit1,
    output bit2,
    output bit3,
    output bit4,
    output bit5,
    output bit6
);

    assign bit0 = ~word_in[0]; // Assign each bit from the input word to an individual output
    assign bit1 = ~word_in[1];
    assign bit2 = ~word_in[2];
    assign bit3 = ~word_in[3];
    assign bit4 = ~word_in[4];
    assign bit5 = ~word_in[5];
    assign bit6 = ~word_in[6];

endmodule
*/
