// Digital circuit jogo_desafio_memoria_simulacao.dig as structural Verilog
module jogo_desafio_memoria_simulacao (
  input  Clock_1KHz,
  input  dificuldada,
  output Igual,
  output [6:0] Contagem,
  output [6:0] Memoria,
  output [6:0] Estado,
  output [6:0] JogadaFeita,
  output dbClock,
  output dbIniciar,
  output TemJogada,
  output [6:0] Limite,
  output dificuldade,
  output [1:0] SelMux
);

  wire bussplitter_1_d0, bussplitter_1_d1, bussplitter_1_d2, bussplitter_1_d3, Chave0_out, Chave1_out,
       Chave2_out, Chave3_out, Iniciar_out, Reset_out, u_jogo_desafio_memoria_ganhou,
       u_jogo_desafio_memoria_perdeu, u_jogo_desafio_memoria_pronto, u_jogo_desafio_memoria_timeout,
       u_Split7Bit_2_bit0, u_Split7Bit_2_bit1, u_Split7Bit_2_bit2, u_Split7Bit_2_bit3, u_Split7Bit_2_bit4,
       u_Split7Bit_2_bit5, u_Split7Bit_2_bit6, u_Split7Bit_3_bit0, u_Split7Bit_3_bit1, u_Split7Bit_3_bit2,
       u_Split7Bit_3_bit3, u_Split7Bit_3_bit4, u_Split7Bit_3_bit5, u_Split7Bit_3_bit6, u_Split7Bit_4_bit0,
       u_Split7Bit_4_bit1, u_Split7Bit_4_bit2, u_Split7Bit_4_bit3, u_Split7Bit_4_bit4, u_Split7Bit_4_bit5,
       u_Split7Bit_4_bit6, u_Split7Bit_5_bit0, u_Split7Bit_5_bit1, u_Split7Bit_5_bit2, u_Split7Bit_5_bit3,
       u_Split7Bit_5_bit4, u_Split7Bit_5_bit5, u_Split7Bit_5_bit6, u_Split7Bit_bit0, u_Split7Bit_bit1,
       u_Split7Bit_bit2, u_Split7Bit_bit3, u_Split7Bit_bit4, u_Split7Bit_bit5, u_Split7Bit_bit6;
  wire [3:0] u_jogo_desafio_memoria_leds, u_jointBit_chaves_out;

  Button Chave0 (.out(Chave0_out));
  Button Chave1 (.out(Chave1_out));
  Button Chave2 (.out(Chave2_out));
  Button Chave3 (.out(Chave3_out));
  jointBit #(.applicationType("IVERILOG")) u_jointBit (
    .chaves0(Chave0_out), .chaves1(Chave1_out), .chaves2(Chave2_out), .chaves3(Chave3_out),
    .chaves_out(u_jointBit_chaves_out));
  Split7Bit #(.applicationType("IVERILOG")) u_Split7Bit (
    .word_in(Limite), .bit0(u_Split7Bit_bit0), .bit1(u_Split7Bit_bit1), .bit2(u_Split7Bit_bit2),
    .bit3(u_Split7Bit_bit3), .bit4(u_Split7Bit_bit4), .bit5(u_Split7Bit_bit5), .bit6(u_Split7Bit_bit6));
  Button Reset (.out(Reset_out));
  Button Iniciar (.out(Iniciar_out));
  jogo_desafio_memoria #(.applicationType("IVERILOG"), .CodeFile("/home/thaylor/Poli/labdig/LabDig-Aulas/exp6/simulacao/jogo_memoria_combined.v")) u_jogo_desafio_memoria (
    .clock(Clock_1KHz), .reset(Reset_out), .jogar(Iniciar_out), .botaoDificuldade(dificuldada),
    .botoes(u_jointBit_chaves_out), .leds(u_jogo_desafio_memoria_leds),
    .ganhou(u_jogo_desafio_memoria_ganhou), .perdeu(u_jogo_desafio_memoria_perdeu),
    .pronto(u_jogo_desafio_memoria_pronto), .timeout(u_jogo_desafio_memoria_timeout), .db_contagem(Contagem),
    .db_memoria(Memoria), .db_estado(Estado), .db_jogadafeita(JogadaFeita), .db_limite(Limite),
    .db_clock(dbClock), .db_igual(Igual), .db_iniciar(dbIniciar), .db_tem_jogada(TemJogada),
    .db_dificuldade(dificuldade), .db_selMux(SelMux));
  Seven_Seg seven_seg_1 (
    .a(u_Split7Bit_bit0), .b(u_Split7Bit_bit1), .c(u_Split7Bit_bit2), .d(u_Split7Bit_bit3),
    .e(u_Split7Bit_bit4), .f(u_Split7Bit_bit5), .g(u_Split7Bit_bit6), .dp(1'b0));
  Split7Bit #(.applicationType("IVERILOG")) u_Split7Bit_2 (
    .word_in(JogadaFeita), .bit0(u_Split7Bit_2_bit0), .bit1(u_Split7Bit_2_bit1), .bit2(u_Split7Bit_2_bit2),
    .bit3(u_Split7Bit_2_bit3), .bit4(u_Split7Bit_2_bit4), .bit5(u_Split7Bit_2_bit5), .bit6(u_Split7Bit_2_bit6));
  Seven_Seg seven_seg_2 (
    .a(u_Split7Bit_2_bit0), .b(u_Split7Bit_2_bit1), .c(u_Split7Bit_2_bit2), .d(u_Split7Bit_2_bit3),
    .e(u_Split7Bit_2_bit4), .f(u_Split7Bit_2_bit5), .g(u_Split7Bit_2_bit6), .dp(1'b0));
  LED Acertou (.in(u_jogo_desafio_memoria_ganhou));
  LED Errou (.in(u_jogo_desafio_memoria_perdeu));
  LED Pronto (.in(u_jogo_desafio_memoria_pronto));
  LED dbTimeout (.in(u_jogo_desafio_memoria_timeout));
  Split7Bit #(.applicationType("IVERILOG")) u_Split7Bit_3 (
    .word_in(Estado), .bit0(u_Split7Bit_3_bit0), .bit1(u_Split7Bit_3_bit1), .bit2(u_Split7Bit_3_bit2),
    .bit3(u_Split7Bit_3_bit3), .bit4(u_Split7Bit_3_bit4), .bit5(u_Split7Bit_3_bit5), .bit6(u_Split7Bit_3_bit6));
  BusSplitter #(.Bits(4)) bussplitter_1 (
    .D(u_jogo_desafio_memoria_leds), .OE(1'b1), .D0(bussplitter_1_d0), .D1(bussplitter_1_d1),
    .D2(bussplitter_1_d2), .D3(bussplitter_1_d3));
  LED led_1 (.in(bussplitter_1_d0));
  LED led_2 (.in(bussplitter_1_d1));
  LED led_3 (.in(bussplitter_1_d2));
  LED led_4 (.in(bussplitter_1_d3));
  Split7Bit #(.applicationType("IVERILOG")) u_Split7Bit_4 (
    .word_in(Memoria), .bit0(u_Split7Bit_4_bit0), .bit1(u_Split7Bit_4_bit1), .bit2(u_Split7Bit_4_bit2),
    .bit3(u_Split7Bit_4_bit3), .bit4(u_Split7Bit_4_bit4), .bit5(u_Split7Bit_4_bit5), .bit6(u_Split7Bit_4_bit6));
  Seven_Seg seven_seg_3 (
    .a(u_Split7Bit_3_bit0), .b(u_Split7Bit_3_bit1), .c(u_Split7Bit_3_bit2), .d(u_Split7Bit_3_bit3),
    .e(u_Split7Bit_3_bit4), .f(u_Split7Bit_3_bit5), .g(u_Split7Bit_3_bit6), .dp(1'b0));
  Split7Bit #(.applicationType("IVERILOG")) u_Split7Bit_5 (
    .word_in(Contagem), .bit0(u_Split7Bit_5_bit0), .bit1(u_Split7Bit_5_bit1), .bit2(u_Split7Bit_5_bit2),
    .bit3(u_Split7Bit_5_bit3), .bit4(u_Split7Bit_5_bit4), .bit5(u_Split7Bit_5_bit5), .bit6(u_Split7Bit_5_bit6));
  Seven_Seg seven_seg_4 (
    .a(u_Split7Bit_4_bit0), .b(u_Split7Bit_4_bit1), .c(u_Split7Bit_4_bit2), .d(u_Split7Bit_4_bit3),
    .e(u_Split7Bit_4_bit4), .f(u_Split7Bit_4_bit5), .g(u_Split7Bit_4_bit6), .dp(1'b0));
  Seven_Seg seven_seg_5 (
    .a(u_Split7Bit_5_bit0), .b(u_Split7Bit_5_bit1), .c(u_Split7Bit_5_bit2), .d(u_Split7Bit_5_bit3),
    .e(u_Split7Bit_5_bit4), .f(u_Split7Bit_5_bit5), .g(u_Split7Bit_5_bit6), .dp(1'b0));

  // Notes on the sheet:
  //   Clock_1KHz: Hz: 1000
endmodule

/* Code of jointBit:
module jointBit (
    input chaves0,
    input chaves1,
    input chaves2,
    input chaves3,
    output [3:0] chaves_out
);

	assign chaves_out = {chaves3, chaves2, chaves1, chaves0};

endmodule
*/

/* Code of Split7Bit:
module Split7Bit (
    input [6:0] word_in,      // 7-bit input
    output bit0,              // Outputs individual bits
    output bit1,
    output bit2,
    output bit3,
    output bit4,
    output bit5,
    output bit6
);

    assign bit0 = ~word_in[0]; // Assign each bit from the input word to an individual output
    assign bit1 = ~word_in[1];
    assign bit2 = ~word_in[2];
    assign bit3 = ~word_in[3];
    assign bit4 = ~word_in[4];
    assign bit5 = ~word_in[5];
    assign bit6 = ~word_in[6];

endmodule
*/
